# Fritzing sketch cf-arduino-soil-moisture (saved by Fritzing 0.8.7b)

parts:
  U1 = ESP8266 NodeMCU LoLin module
  Capacitive_Soil_Moisture_Sensor1 = DFRobot Capacitive Soil Moisture Sensor V1.0 [part_number=SEN0193]

nets:
  3V3: U1.3V3, Capacitive_Soil_Moisture_Sensor1.VCC
  GND: U1.GND, Capacitive_Soil_Moisture_Sensor1.GND
  N1: U1.A0, Capacitive_Soil_Moisture_Sensor1.A

custom parts:
  ESP8266 NodeMCU LoLin module: ESP8266 based NodeMCU
  DFRobot Capacitive Soil Moisture Sensor V1.0: DFRobot Capacitive Soil Moisture Sensor V1.0 This product measures soil moisture levels by capacitive sensing, rather than resistive sensing like other types of moisture sensor. It is made of a corrosion resistant material giving it a long service life. Insert it into soil and impress your friends with the real-time soil moisture data! The product includes an on-board voltage regulator which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
